# Fritzing sketch game (saved by Fritzing 0.9.2b)
breadboards: 1

parts:
  Part1 = Photon
  Part2 = Thumb Joystick

nets:
  N1: Part1.A1, Part2.HORZ
  N2: Part1.A2, Part2.VERT
  GND: Part1.GND, Part2.GND
  3V3: Part1.3V3, Part2.VCC
