# Fritzing sketch task2 (saved by Fritzing 0.9.2b)
breadboards: 1

parts:
  Part1 = Photon
  S1 = Pushbutton [package="[THT]"]
  R1 = Resistor [tolerance=±5% resistance=220 package=THT]

nets:
  N1: Part1.GND, R1.Pin_0
  N2: Part1.D2, S1.Pin_1, S1.Pin_2, R1.Pin_1
  N3: Part1.3V3, S1.Pin_3, S1.Pin_4
