# Fritzing sketch task4 (saved by Fritzing 0.9.2b)
breadboards: 1

parts:
  Part1 = Photon
  R1 = Resistor [tolerance=±5% resistance=220 package=THT]
  R2 = Photocell (LDR) [package=THT]

nets:
  N1: Part1.A2, R1.Pin_1, R2.pin_0
  N2: Part1.GND, R2.pin_1
  N3: Part1.3V3, R1.Pin_0
