# Fritzing sketch task9 (saved by Fritzing 0.9.2b)
breadboards: 1

parts:
  Part1 = Photon
  R1 = PHOTOCELL [package=photocell-kit]
  R2 = Resistor [tolerance=±5% resistance=220 package=THT]
  KY-008_Laserdiode2 = Laser [part_number=1219301 package=keys]

nets:
  N1: Part1.A0, R1.P$1, R2.Pin_1
  N2: Part1.GND, R1.P$2, KY-008_Laserdiode2.connector2pin
  N3: Part1.D5, KY-008_Laserdiode2.connector0pin
  N4: Part1.3V3, R2.Pin_0, KY-008_Laserdiode2.connector1pin

custom parts:
  Laser: KEYES KY-008 650nm Laser Transmitter Module
